# Fritzing sketch useless-box (saved by Fritzing 0.9.2b)

parts:
  S1 = Toggle Switch [package=THT]
  J2 = Basic Servo [part_number=flag]
  J3 = Basic Servo [part_number=arm]
  M1 = DC Motor [part_number=Movement]
  Part2 = Arduino Motor Shield (Rev3) [part_number="UNO + Motor Shield"]
  IC1 = Voltage Regulator [part_number=UBEC package=to220-igo]
  U1 = LIPO-2000mAh [package=lipo-2000]
  J4 = Basic Servo [part_number=door]
  J5 = Infrared Proximity Sensor
  R1 = Resistor [tolerance=±5% resistance=10k package="0402 [SMD]"]

nets:
  5V: S1.COM, Part2.5V, J5.Vcc
  N1: S1.L2, Part2.D2, R1.Pin_0
  GND: J2.gnd, J3.gnd, Part2.GND, IC1.GND, U1.-, J4.gnd, J5.GND, R1.Pin_1
  VCC: J2.vcc, J3.vcc, IC1.OUT, J4.vcc
  N2: J2.pulse, Part2.D10_PWM
  N3: J3.pulse, Part2.D3_PWM/A
  N4: M1.pin_1, Part2.B+
  N5: M1.pin_2, Part2.B-
  N6: Part2.A4, J5.Vout
  N7: Part2.D5_PWM, J4.pulse
  N8: Part2.VMOT, IC1.IN, U1.+

// code stored in the sketch: useless-box.ino
#define ENABLE_PRINT

#ifdef ENABLE_PRINT
  #define Sprintln(a) (Serial.println(a))
  #define Sprint(a) (Serial.print(a))
  #define Sbegin(a) (Serial.begin(a))
#else   
  #define Sprintln(a)
  #define Sprint(a)
  #define Sbegin(a)
#endif

#include <Servo.h>
#include <Bounce2.h>

#include "MotorControl.h"
#include "ServoControl.h"

/*
 * Servo positions
 */ 
#define MIN_ARM_DEG 35
#define MAX_ARM_DEG 165
#define POS_ARM_HOME MIN_ARM_DEG
#define POS_SWITCH_ARM MAX_ARM_DEG
#define POS_ARM_PEEK (MIN_ARM_DEG + 70)
#define POS_ARM_CHECK_NINJA (MIN_ARM_DEG + 20) 
#define POS_ARM_NEAR_SWITCH (MAX_ARM_DEG - 50)

#define MIN_DOOR_DEG 100
#define MAX_DOOR_DEG 40
#define POS_DOOR_HOME MIN_DOOR_DEG
#define POS_DOOR_MEDIUM_OPEN (POS_DOOR_HOME - 30) //TODO medium is low and ninja is very high open... not really good, ninja should be so low that the arm has to push through the door
#define POS_DOOR_FULL_OPEN MAX_DOOR_DEG
#define POS_DOOR_CHECK_NINJA (POS_DOOR_HOME - 70)
#define POS_DOOR_FLAP POS_DOOR_HOME - 20

#define MIN_FLAG_DEG 60
#define MAX_FLAG_DEG 160
#define POS_FLAG_HIDDEN MIN_FLAG_DEG
#define POS_FLAG_RAISED MAX_FLAG_DEG
#define POS_FLAG_TILTED (MAX_FLAG_DEG - 40)

// the number of msec (approx.) for the servo to go one degree further
#define MECANIC_SPEED_PER_DEGREE 2  // 2 msec to move 1 degree
// the delay between the arm hitting the switcha and the switch reporting a change in value 
#define MECANIC_DELAY_SWITCH 70     // 70 msec to acknowledge a hit

#define IMPATIENT_INTERVAL_THRESHOLD 5  //times the interval must be triggered before impatient mode is activated
const long IMPATIENT_INTERVAL_TIME = 20000;
#define NUM_MAX_IMPATIENT_ACTION 7      //number of impatient actions - while the box stays in impatient mode

#define NUM_BEHAVIOURS 19

// Pins
const int armServoPin = 9;
const int doorServoPin = 6;
const int flagServoPin = 5;
const int directionPin = 13;
const int throttlePin = 11;
const int distancePin = A4;
const int boxSwitchPin  = 2;
const int debugPin = 4;

// Operation variables
Bounce bouncer = Bounce();
int activated = LOW;

int selectedBehaviour = 1;            // This is used to choose the next behaviour 
long randCheck = 1;               // Random check when not activated
boolean hasAlreadyChecked = true; // Set when box has checked the switch (peeked at it)
boolean interrupted = false;      // Is set to true when the switch has been changed while doing something. Allows for a quick check in the loop() for what we should do next

//Distance detection
int lastDistance = 0;             // Last measured distance
int threshold = 200;              // Distance threshold
unsigned long timer;              // Distance timer

// Impatient mode variables
int impatientCount = 0;           // How many impatient actions were done
int impatientThresholdCount = 0;  // How may times was the switch operated in short intervals
boolean impatient = false;        // is the box impatient
unsigned long activatedTimestamp; // When was the box last activated

MotorControl motor = MotorControl();
ServoControl arm = ServoControl("arm");
ServoControl door = ServoControl("door");
ServoControl flag = ServoControl("flag");

/**
 * Simple blink method for debug purposes
 */
void debugBlink(int times = 3, int wait = 200) {
  /*int i;
  for (i = 0; i < times; i++) {
    digitalWrite(debugPin, HIGH);
    delay(wait);
    digitalWrite(debugPin, LOW);  
    delay(wait);
  }*/  
}

void setup() {  
  pinMode(boxSwitchPin, INPUT);
  pinMode(directionPin, OUTPUT);  
  pinMode(distancePin,INPUT);
  pinMode(debugPin, OUTPUT);  
  
  Sbegin(9600);
  Sprintln(F("Started.")); 
  Sprintln(F("Initializing positions."));

  bouncer.attach(boxSwitchPin);
  motor.attach(directionPin, throttlePin);
  //distance.attach(2);
  arm.attach(&bouncer, armServoPin, POS_ARM_HOME, POS_SWITCH_ARM);
  door.attach(&bouncer, doorServoPin, POS_DOOR_HOME, POS_DOOR_FULL_OPEN);
  flag.attach(&bouncer, flagServoPin, POS_FLAG_HIDDEN, POS_FLAG_RAISED);
  
  activatedTimestamp = IMPATIENT_INTERVAL_TIME + 1;
 
  //debug - I'm able to detect arduino resets like this...
  debugBlink(3, 1000); 
  randomSeed(analogRead(0));      
}

/**
 * A "soft" delay function - This function can be interrupted by manual switch change.
 * If interrupted the method returns early and sets the interruped state variable to true.
 * The soft delay function returns the value of the switch
 */
int softDelay(int msec) {
  Sprint(F("Delaying for "));
  Sprint(msec);
  Sprintln(F(" msec...")); 
  bouncer.update();
  int val = bouncer.read();
  int current_value;
  long time_counter = 0;  
  do {
    delay(1);
    time_counter++;
    bouncer.update();
    current_value = bouncer.read();
    if (current_value != val) {
      Sprintln(F("/!\\[Soft Delay] Interrupted - The switch was operated while I was waiting on purpose !"));
      interrupted = true;
      break;
    }
  } while(time_counter <= msec);
  return current_value;
}

/**
 * Detect movement inside a given threshold
 */
boolean detect(int detectionTime) {
  int currentDistance;
  delay(1200);    //wait to stabilize sensor readings after opening the door   
  timer = millis();
  // wait for movement that exceeds threshold or if timer expires (5 sec),
  while(millis() - timer <= detectionTime - 1200) {
    currentDistance = analogRead(distancePin);        
    Sprint(F("Current Distance"));
    Sprintln(currentDistance);
    if(currentDistance >= 400) { // The users hand is near the switch!
      Sprintln(F("Detected!"));
      return true;
    }    
    delay(500);
  }
  return false;
}

/**
 * Reset operation to normal mode, reposition arm and door
 */
void resetToNormalMode() {
  Sprintln(F("Getting tired, leaving impatient mode..."));      
  impatientCount = 0;
  impatient = false;
  arm.reattach();
  door.reattach();    
  door.setHome(POS_DOOR_HOME);
  door.isHome(false);
  arm.setHome(POS_ARM_HOME);    
  arm.isHome(false);
}

/**
 * Set operation mode to impation mode, reposition arm and door
 */
void setImpatientMode() {
  Sprintln(F("Alright, thats it! I'm getting impatient!"));
  impatient = true;    
  impatientThresholdCount = 0;     
  arm.isHome(false);
  arm.setHome(POS_ARM_PEEK);      
  door.isHome(false);
  door.setHome(POS_DOOR_MEDIUM_OPEN);            
  delay(100);
}

/**
 * Get the next normal behaviour
 */
int determineNormalBehaviour() {            
  int newBehaviour;
  do {
    newBehaviour = random(1, NUM_BEHAVIOURS);      
  } while (newBehaviour == selectedBehaviour );
  selectedBehaviour = newBehaviour;    
  return newBehaviour;  
}

/**
 * Get the next behaviour for impatient mode
 */
int determineImpatientBehaviour() {     
  int result = 1;
  //define "special" moves
  switch(impatientCount) {
    case NUM_MAX_IMPATIENT_ACTION - 3:
      result = 9; break;
    case NUM_MAX_IMPATIENT_ACTION - 2:
      result = 101; break;
    case NUM_MAX_IMPATIENT_ACTION - 1: 
      result = 100; break;
    case NUM_MAX_IMPATIENT_ACTION:
      result = 102; break;
    default:
      break;
  }  
  return result;
}

/* ------------------------------- */
/* ---- STANDARD BEHAVIOURS ------ */
/* ------------------------------- */

void flipSwitch(int msec = 0) { 
  interrupted = arm.move(POS_SWITCH_ARM, msec); 
  delay(MECANIC_DELAY_SWITCH); // Wait for the switch to acknowledge before returning in the loop
}

// Go near the arm, but not as close as to push the switch, and then retracts a bit
void tryFail(int msec = 0) {  
  interrupted = arm.move(POS_ARM_NEAR_SWITCH, msec);
  interrupted = arm.move(POS_ARM_NEAR_SWITCH + 7, msec); 
}

// Open the lid stealthly. User does not see me. I'm a NINJA !
void goStealthCheck() {    
  interrupted = arm.move(POS_ARM_CHECK_NINJA, 30);
  interrupted = arm.move(POS_ARM_NEAR_SWITCH + 7, 30);  
}

void openDoorNinja(int msec = 0) {
  interrupted = door.move(POS_DOOR_CHECK_NINJA, msec);
}

void openDoorFlap(int msec = 0) {
  interrupted = door.move(POS_DOOR_FLAP, msec);  
}

void openDoorMedium(int msec = 0) {
  interrupted = door.move(POS_DOOR_MEDIUM_OPEN, msec);  
}

void openDoorFull(int msec = 0) {
  interrupted = door.move(POS_DOOR_FULL_OPEN, msec);
}

// Ok, back home now
void backHome() { 
  int homePosArm = impatient ? POS_ARM_PEEK : POS_ARM_HOME;
  arm.move(homePosArm, 0); 
}

// Open the lid to see out
void goCheck(int msec = 0) {  
  interrupted = arm.move(POS_ARM_PEEK, msec); 
}

void closeDoor(int msec = 0) {
  int homePos = impatient ? POS_DOOR_MEDIUM_OPEN : POS_DOOR_HOME;  
  interrupted = door.move(homePos, msec);
}


void raiseflag(int msec = 0) {
  interrupted = flag.move(POS_FLAG_RAISED, msec);
}

void tiltflag(int msec = 0) {
  interrupted = flag.move(POS_FLAG_TILTED, msec);
}

void hideflag(int msec = 0) {
  interrupted = flag.move(POS_FLAG_HIDDEN, msec);  
}

void waveflag(int times) {
  byte i;
  raiseflag();  
  softDelay(100);
  for (i = 0; i < times; i++) {    
    tiltflag();
    softDelay(15);
    raiseflag();    
  }
  softDelay(70);
  hideflag();  
}

/* ------------------------------------ */
/* ---- INTERRUPTABLE BEHAVIOURS ------ */
/* use these for the concrete movements */
/* ------------------------------------ */

// Go out and flip that switch the user just
void goOpenDoorAndFlipThatSwitch(int msec = 0) { 
  if (!interrupted) openDoorMedium(msec);
  if (!interrupted) flipSwitch(msec);
}

void driveAway(){
  if (!interrupted) openDoorMedium();
  if (!interrupted) motor.forward(100);
  if (!interrupted) softDelay(2000);  
  if(!interrupted && detect(3000)) {
    Sprintln(F("Detected movement!"));
    if (!interrupted) motor.forward(100);
    if (!interrupted) softDelay(800);
    if (!interrupted) motor.halt();
  }
  motor.halt();
  if (!interrupted) goOpenDoorAndFlipThatSwitch();  
}

void whiteflag() 
{  
  flag.isHome(false);  
  if (!interrupted) openDoorFull();
  if (!interrupted) waveflag(7);
  if (!interrupted) softDelay(500);
  if (!interrupted) flipSwitch();   
}

// Check once, wait, then flip the switch
void check() {
  if (!interrupted) openDoorMedium();
  if (!interrupted) goCheck(random(0, 10));
  if (!interrupted) softDelay(1000);
  if (!interrupted) goOpenDoorAndFlipThatSwitch();
}

// Check, return back home, then flip
void checkReturn() {
  if (!interrupted) openDoorMedium();
  if (!interrupted) goCheck(random(0,10));
  if (!interrupted) softDelay(1500);
  if (!interrupted) backHome();
  if (!interrupted) softDelay(600);
  if (!interrupted) goOpenDoorAndFlipThatSwitch();
}

// Multi tries. At the end, succeeds...
void multiTry() {
  if (!interrupted) openDoorMedium();
  if (!interrupted) tryFail(5);
  if (!interrupted) softDelay(500);
  if (!interrupted) tryFail(5);
  if (!interrupted) softDelay(500);  
  if (!interrupted) backHome();
  if (!interrupted) softDelay(200);
  if (!interrupted) goOpenDoorAndFlipThatSwitch();
}

// Check once slowly, return, check again, return to stealth position, then flip
void checkCheckReturn() { //not ok
  if (!interrupted) openDoorNinja(30);
  if (!interrupted) openDoorMedium();
  if (!interrupted) goStealthCheck();
  if (!interrupted) softDelay(1000);
  if (!interrupted) backHome();
  if (!interrupted) closeDoor();
  if (!interrupted) openDoorMedium();
  if (!interrupted) goCheck(10);
  if (!interrupted) backHome();
  if (!interrupted) closeDoor();
  if (!interrupted) softDelay(700);
  if (!interrupted) openDoorNinja(30);
  if (!interrupted) goStealthCheck();
  if (!interrupted) softDelay(500);
  if (!interrupted) goOpenDoorAndFlipThatSwitch();
}

void afraid() {
  if (!interrupted) openDoorMedium();
  if (!interrupted) tryFail();  
  if (!interrupted) goCheck();
  if (!interrupted) backHome();
  if (!interrupted) closeDoor();
  if (!interrupted) softDelay(1000);
  if (!interrupted) openDoorMedium();
  if (!interrupted) flipSwitch(5);
}

// #OhWait 
void ohWait() {
  if (!interrupted) openDoorMedium();
  if (!interrupted) tryFail();
  if (!interrupted) backHome();
  if (!interrupted) openDoorMedium();
  if (!interrupted) softDelay(700);
  if (!interrupted) goCheck(2); // Woops. Forgot something ?
  if (!interrupted) softDelay(1000);
  if (!interrupted) goOpenDoorAndFlipThatSwitch(15);
}

void matrix() {
  if (!interrupted) openDoorMedium();
  if (!interrupted) goCheck(10);  
  if (!interrupted) flipSwitch(30);
  if (!interrupted) softDelay(300);  
}

void crazyDoor() {
  if (!interrupted) openDoorMedium(7);
  if (!interrupted) closeDoor();
  if (!interrupted) softDelay(700);
  if (!interrupted) openDoorFull();    
  if (!interrupted) softDelay(500);  
  if (!interrupted) closeDoor();  
  if (!interrupted) openDoorFull();      
  if (!interrupted) flipSwitch(15);  
}

void crazySlow() { //ok  
  if (!interrupted) goOpenDoorAndFlipThatSwitch(30);  
}

void flappingAround() {
  int i;
  for(i = 0; i < 5; i++) {
    if (!interrupted) openDoorFull(10);
    if (!interrupted) closeDoor();    
    if (!interrupted) softDelay(200);         
  }
  if (!interrupted) goOpenDoorAndFlipThatSwitch();   
}

void lowFlappingAround() {
  int i;
  for(i = 0; i < 5; i++) {
    if (!interrupted) openDoorFlap(0);
    if (!interrupted) closeDoor();        
  }  
  if (!interrupted) softDelay(300);         
  if (!interrupted) goOpenDoorAndFlipThatSwitch();   
}

void vibrating() {
  if (!interrupted) openDoorMedium();
  if (!interrupted) tryFail();  
  if (!interrupted) tryFail();
  if (!interrupted) tryFail();
  if (!interrupted) tryFail();
  if (!interrupted) tryFail();
  if (!interrupted) tryFail();
  if (!interrupted) tryFail();
  if (!interrupted) backHome();
  if (!interrupted) goOpenDoorAndFlipThatSwitch();  
}

void moveBackAndForth() {  
  if (!interrupted) motor.forward(100);
  if (!interrupted) softDelay(600); 
  if (!interrupted) motor.backward(100);
  if (!interrupted) softDelay(600); 
  if (!interrupted) motor.forward(100);  
  if (!interrupted) softDelay(600); 
  if (!interrupted) motor.backward(100);
  if (!interrupted) softDelay(600); 
  if(!interrupted && detect(3000)) {
    Sprintln(F("Detected movement!"));
    if (!interrupted) motor.forward(100);
    if (!interrupted) softDelay(300);
    if (!interrupted) motor.halt();
  }  
  motor.halt();
  if (!interrupted) openDoorNinja(30);  
  if (!interrupted) goOpenDoorAndFlipThatSwitch();  
}

void turnOffThenWait() {  
  arm.interruptable(false);
  if (!interrupted) goOpenDoorAndFlipThatSwitch(0);
  if (!interrupted) goCheck();
  arm.interruptable(true);
  if (!interrupted) softDelay(2000);  
}

void turnOffwaitAndFlipDoor() {
  arm.interruptable(false);
  if (!interrupted) goOpenDoorAndFlipThatSwitch(0);  
  int i;
  for(i = 0; i < 3; i++) {
    if (!interrupted) openDoorFull(0);    
    if (!interrupted) openDoorMedium(7);      
  }  
  arm.interruptable(true);  
  if (!interrupted) softDelay(500);    
}

void angryTurnOff() {
  arm.interruptable(false);
  goOpenDoorAndFlipThatSwitch();  
  backHome();
  goOpenDoorAndFlipThatSwitch();  
  backHome();
  goOpenDoorAndFlipThatSwitch();
  arm.move(POS_ARM_HOME, 0);
  arm.interruptable(true);
  if (!interrupted) softDelay(300);
  flag.isHome(false);  
  openDoorFull();
  waveflag(7);  
  flipSwitch();
}

/**
 * TODO when user is detected
 * 1. drive away
 * 2. flap door
 * 3. ??
 * 
 */
//working debug test
void turnOffIfUserIsDetected() {
  int i;
  for (i = 0; i < random(3, 5); i++) {
    openDoorMedium(15);
    flipSwitch();
    backHome();    
    if (detect(10000)) {
      goCheck(random(0, 30));           
      if(softDelay(5000) == LOW) {
        break;    
      }      
    }
  }  
}

void randomCheck() {
  hasAlreadyChecked = true;
  arm.isHome(false);         
  if (!interrupted) arm.reattach();
  if (!interrupted) door.reattach();            
  if (!interrupted) goCheck(5);
  if (!interrupted) softDelay(1000);      
}


void loop() {
  // Update the switch position
  bouncer.update();
  activated = bouncer.read();  

  //do i need this?
  /*if (flag.isHome() == false) {    
    Sprintln(F("Hiding flag"));
    hideflag();        
  } else*/
  if (arm.isHome() == false) {    
    Sprintln(F("Going back home"));
    backHome();        
  } else if (door.isHome() == false) {
    Sprintln(F("Closing door"));
    closeDoor();     
  } else if (randCheck < 5 && hasAlreadyChecked == false) {                
    Sprintln(F("Random check, baby. "));            
    randomCheck();
  }  else if (activated == HIGH) {    
    Sprintln(F("Who turned me on?"));
    
    arm.isHome(false);
    door.isHome(false);
    
    arm.reattach();
    door.reattach();
    flag.reattach();
       
    if(impatient) {
      Sprint(F("I'm impatient right now - for the "));       
      impatientCount++;
      Sprint(impatientCount);
      Sprintln(F(" time!"));
    } else if (!impatient && (millis() - activatedTimestamp <= IMPATIENT_INTERVAL_TIME)) { 
      //increase impatient trigger count if box is operated repeatedly in interval
      //     
      //TODO activate threshold as soon as fixed standalone problem    
      impatientThresholdCount++;
      Sprint(F("Getting impatient... "));
      Sprint(impatientThresholdCount);
      Sprint(F(" of "));
      Sprintln(IMPATIENT_INTERVAL_THRESHOLD);
      Sprint(F("Time difference is: "));
      Sprintln(millis() - activatedTimestamp);
      debugBlink(impatientThresholdCount);      
    }
    
    //update activated after impatient check
    activatedTimestamp = millis();

    // set to impatient mode if conditions are met
    if (!impatient && impatientThresholdCount >= IMPATIENT_INTERVAL_THRESHOLD ) {
      setImpatientMode();
      //TODO: Debug led, remove
      debugBlink(5, 70);  
      digitalWrite(debugPin, HIGH);
    }

    //use specific moves in impatient mode 
    if (impatient) {
      selectedBehaviour = determineImpatientBehaviour();    
    } else {      
      selectedBehaviour  = determineNormalBehaviour();
    }    

        //reset to normal mode after NUM_MAX_IMPATIENT_ACTION actions have been performed;
    if(impatient && impatientCount >= NUM_MAX_IMPATIENT_ACTION) { 
      //TODO: Debug led, remove
      debugBlink(5, 70);  
      digitalWrite(debugPin, LOW);
      resetToNormalMode(); 
    }  

    Sprint(F("-------- Starting behaviour: ["));
    Sprint(selectedBehaviour);
    Sprintln(F("]"));
    Sprint(F("-------- "));
    switch(selectedBehaviour) { 
      case 1: 
        Sprintln(F("Normal flip"));
        goOpenDoorAndFlipThatSwitch(); break;
      case 2: 
        Sprintln(F("Check"));  
        check(); break;
      case 3: 
        Sprintln(F("Multi try"));
        multiTry(); break;
      case 4: 
        Sprintln(F("Check and return"));
        checkReturn(); break;
      case 5: 
        Sprintln(F("Check, check and return"));
        checkCheckReturn(); break;
      case 6: 
        Sprintln(F("Afraid"));
        afraid(); break;
      case 7: 
        Sprintln(F("Oh, wait"));
        ohWait(); break;
      case 8: 
        Sprintln(F("Crazy slow"));
        crazySlow(); break;        
      case 9: 
        Sprintln(F("Matrix"));
        matrix(); break;
      case 10: 
        Sprintln(F("Crazy door"));
        crazyDoor(); break;
      case 11: 
        Sprintln(F("Drive away"));
        driveAway(); break;      
      case 12:
        Sprintln(F("Back and Forth"));
        moveBackAndForth(); break;
      case 14:
        Sprintln(F("low flapping around"));
        lowFlappingAround(); break;  
      case 15:
        Sprintln(F("turn off, wait"));
        turnOffThenWait(); break;  
      case 16:
        Sprintln(F("long wait after turnoff"));
        turnOffwaitAndFlipDoor(); break; 
      case 17: //should i really include this in the normal operaion mode? it's a special gimick      
        Sprintln(F("White flag"));
        whiteflag(); break;         
      case 18:
        Sprintln(F("Measure Distance"));
        turnOffIfUserIsDetected(); break;    
      case 100:
        Sprintln(F("Vibrating"));      
        vibrating(); break;  
      case 101:
        Sprintln(F("Flapping door around"));
        flappingAround(); break;      
      case 102:
        Sprintln(F("Angry turn-off"));
        angryTurnOff(); break;
      default: 
        Sprintln(F("Default"));
        goOpenDoorAndFlipThatSwitch(); break;   
      } 
      //reset the interrupted state - i'm done now...
      interrupted = false; 
  } // end switch-if
   
  arm.waitAndDetatch();
  door.waitAndDetatch();
  flag.waitAndDetatch();  
  //Sprintln(F("end of loop, all detatched..."));
  
  randCheck = random(1, 500000);  
}
